// Logisim project Project5final.circ as structural Verilog: 15 circuits, main circuit regfile
module Computer (
);

  wire buzzer_1_p2, buzzer_2_p2, buzzer_3_p2, buzzer_4_p2, buzzer_4_p4, clock_1_out, clock_2_out,
       clock_3_out, cpu_1_buswriteenable, keyboard_1_avail, keyboardcontroller_1_buswriteenable,
       keyboardcontroller_1_keyboardread, memorycontroller_1_writeenabletomem, memorycontroller_1_writetobus,
       rgb_video_1_p1, rgb_video_1_p2, rgbledcontrol_1_blue, rgbledcontrol_1_green, rgbledcontrol_1_red,
       speakercontroller_1_playmusic, terminalcontroller_1_writetoterminal;
  wire [1:0] speakercontroller_1_toneselect;
  wire [3:0] hexdisplaycontroller_1_datatoscreen;
  wire [6:0] buzzer_1_p3, keyboard_1_data, terminalcontroller_1_datatoterminal;
  wire [7:0] rgb_video_1_p3, rgb_video_1_p4;
  wire [13:0] buzzer_1_p1;
  wire [23:0] memorycontroller_1_addresstomem, rgb_video_1_p5;
  wire [25:0] cpu_1_addresstobus;
  wire [31:0] controlled_buffer_1_out, cpu_1_datatobus, keyboardcontroller_1_datatobus,
       memorycontroller_1_datatobus, memorycontroller_1_datatomem, ram_1_dout;

  RAM #(.addrWidth(24), .dataWidth(32), .enables("line")) ram_1 (
    .addr(memorycontroller_1_addresstomem), .we(memorycontroller_1_writeenabletomem), .clk(clock_1_out),
    .din(memorycontroller_1_datatomem), .dout(ram_1_dout));
  Clock clock_1 (.out(clock_1_out));
  // Probe on memorycontroller_1_datatomem
  Clock clock_2 (.out(clock_2_out));
  Keyboard #(.buflen(256)) keyboard_1 (
    .clk(clock_2_out), .re(keyboardcontroller_1_keyboardread), .avail(keyboard_1_avail),
    .data(keyboard_1_data));  // open: clr
  Bit_Extender #(.in_width(32), .out_width(2)) bit_extender_1 ();  // open: in, out
  // Probe on controlled_buffer_1_out
  MemoryController memorycontroller_1 (
    .WriteEnableFromBus(cpu_1_buswriteenable), .DataFromBus(controlled_buffer_1_out),
    .DataFromMem(ram_1_dout), .AddressFromBus(cpu_1_addresstobus),
    .AddressToMem(memorycontroller_1_addresstomem), .DataToMem(memorycontroller_1_datatomem),
    .WriteToBus(memorycontroller_1_writetobus), .WriteEnableToMem(memorycontroller_1_writeenabletomem),
    .DataToBus(memorycontroller_1_datatobus));
  CPU cpu_1 (
    .DataFromBus(controlled_buffer_1_out), .DataToBus(cpu_1_datatobus), .AddressToBus(cpu_1_addresstobus),
    .BusWriteEnable(cpu_1_buswriteenable));
  KeyboardController keyboardcontroller_1 (
    .AddressFromBus(cpu_1_addresstobus), .KeyboardStatus(keyboard_1_avail),
    .WriteEnableFromBus(cpu_1_buswriteenable), .KeyboardData(keyboard_1_data),
    .DataFromBus(controlled_buffer_1_out), .DataToBus(keyboardcontroller_1_datatobus),
    .KeyboardRead(keyboardcontroller_1_keyboardread), .BusWriteEnable(keyboardcontroller_1_buswriteenable));
  HexDisplayController hexdisplaycontroller_1 (
    .WriteEnableFromBus(cpu_1_buswriteenable), .DataFromBus(controlled_buffer_1_out),
    .AddressFromBus(cpu_1_addresstobus), .DataToScreen(hexdisplaycontroller_1_datatoscreen));
  assign controlled_buffer_1_out = memorycontroller_1_writetobus ? memorycontroller_1_datatobus : 32'bz;  // Controlled_Buffer controlled_buffer_1
  assign controlled_buffer_1_out = cpu_1_buswriteenable ? cpu_1_datatobus : 32'bz;  // Controlled_Buffer controlled_buffer_2
  assign controlled_buffer_1_out = keyboardcontroller_1_buswriteenable ? keyboardcontroller_1_datatobus : 32'bz;  // Controlled_Buffer controlled_buffer_3
  Hex_Digit_Display hex_digit_display_1 (.value(hexdisplaycontroller_1_datatoscreen));  // open: dp
  // Buzzer buzzer_1: pin names not known; wires that end beside it: buzzer_1_p1, buzzer_1_p2, buzzer_1_p3
  // Probe on cpu_1_addresstobus
  // Probe on cpu_1_buswriteenable
  Clock clock_3 (.out(clock_3_out));
  TTY tty_1 (
    .data(terminalcontroller_1_datatoterminal), .clk(clock_3_out), .we(terminalcontroller_1_writetoterminal));  // open: clr
  // RGB_Video #(.height(256), .scale(1), .width(256)) rgb_video_1: pin names not known; wires that end beside it: rgb_video_1_p1, rgb_video_1_p2, rgb_video_1_p3, rgb_video_1_p4, rgb_video_1_p5
  Clock clock_4 (.out(rgb_video_1_p1));
  // Buzzer #(.waveform("Square")) buzzer_2: pin names not known; wires that end beside it: buzzer_1_p1, buzzer_2_p2, buzzer_1_p3
  // Buzzer #(.waveform("Triangle")) buzzer_3: pin names not known; wires that end beside it: buzzer_1_p1, buzzer_3_p2, buzzer_1_p3
  // Buzzer #(.waveform("Sawtooth")) buzzer_4: pin names not known; wires that end beside it: buzzer_1_p1, buzzer_4_p2, buzzer_1_p3, buzzer_4_p4
  SpeakerController speakercontroller_1 (
    .DataFromBus(controlled_buffer_1_out), .AddressFromBus(cpu_1_addresstobus),
    .WriteEnabled(cpu_1_buswriteenable), .PlayMusic(speakercontroller_1_playmusic),
    .ToneSelect(speakercontroller_1_toneselect), .Hz(buzzer_1_p1), .Volume(buzzer_1_p3));
  TerminalController terminalcontroller_1 (
    .DataFromBus(controlled_buffer_1_out), .WriteEnableFromBus(cpu_1_buswriteenable),
    .AddressFromBus(cpu_1_addresstobus), .WriteToTerminal(terminalcontroller_1_writetoterminal),
    .DataToTerminal(terminalcontroller_1_datatoterminal));
  RGBController rgbcontroller_1 (
    .AddressFromBus(cpu_1_addresstobus), .WriteEnable(cpu_1_buswriteenable),
    .DataFromBus(controlled_buffer_1_out), .RGBWrite(rgb_video_1_p2), .RGBX(rgb_video_1_p3),
    .RGBY(rgb_video_1_p4), .RGBColor(rgb_video_1_p5));
  RGBLEDControl rgbledcontrol_1 (
    .AddressFromBus(cpu_1_addresstobus), .WriteEnable(cpu_1_buswriteenable),
    .DataFromBus(controlled_buffer_1_out), .Green(rgbledcontrol_1_green), .Red(rgbledcontrol_1_red),
    .Blue(rgbledcontrol_1_blue));
  Clock clock_5 (.out(buzzer_4_p4));
  Demultiplexer #(.select(2)) demultiplexer_1 (
    .out0(buzzer_4_p2), .out1(buzzer_3_p2), .out2(buzzer_2_p2), .out3(buzzer_1_p2),
    .in(speakercontroller_1_playmusic), .sel(speakercontroller_1_toneselect));
  // RGBLED rgbled_1: pin names not known; wires that end beside it: rgbledcontrol_1_red, rgbledcontrol_1_green, rgbledcontrol_1_blue

  // Notes on the sheet:
  //   Write_enable
  //   Address
  //   Data
endmodule

module MemoryController (
  input  WriteEnableFromBus,
  input  [25:0] AddressFromBus,
  input  [31:0] DataFromBus,
  input  [31:0] DataFromMem,
  output WriteToBus,
  output WriteEnableToMem,
  output [23:0] AddressToMem,
  output [31:0] DataToMem,
  output [31:0] DataToBus
);

  wire comparator_1_lt, comparator_2_eq, not_1_out, or_1_out;
  wire [25:0] multiplexer_1_out, shifter_1_out;

  // Probe on 26'h3fff004
  Comparator #(.mode("unsigned"), .width(26)) comparator_1 (
    .a(AddressFromBus), .b(26'h3ffff00), .lt(comparator_1_lt));  // open: gt, eq
  Comparator #(.mode("unsigned"), .width(26)) comparator_2 (
    .a(AddressFromBus), .b(26'h3fff004), .eq(comparator_2_eq));  // open: gt, lt
  not not_1 (not_1_out, WriteEnableFromBus);
  Multiplexer #(.width(26)) multiplexer_1 (
    .in0(AddressFromBus), .in1(AddressFromBus), .out(multiplexer_1_out), .sel(comparator_1_lt));
  or or_1 (or_1_out, comparator_1_lt, comparator_2_eq);
  and and_1 (WriteToBus, not_1_out, or_1_out);
  and and_2 (WriteEnableToMem, WriteEnableFromBus, or_1_out);
  Clock clock_1 ();  // open: out
  Shifter #(.shift("lr"), .width(26)) shifter_1 (.in(multiplexer_1_out), .\dist (5'b00010), .out(shifter_1_out));
  // Probe on shifter_1_out
  Bit_Extender #(.in_width(26), .out_width(24)) bit_extender_1 (.in(shifter_1_out), .out(AddressToMem));

  assign DataToBus = DataFromMem;
  assign DataToMem = DataFromBus;
endmodule

module KeyboardController (
  input  [31:0] DataFromBus,
  input  WriteEnableFromBus,
  input  [25:0] AddressFromBus,
  input  KeyboardStatus,
  input  [6:0] KeyboardData,
  output KeyboardRead,
  output BusWriteEnable,
  output [31:0] DataToBus
);

  wire [1:0] comparator_1_eq;
  wire [31:0] bit_extender_1_out, bit_extender_2_out;

  Comparator #(.width(26)) comparator_1 (.a(AddressFromBus), .b(26'h3ffff10), .eq(comparator_1_eq[0]));  // open: gt, lt
  // Probe on 26'h3ffff14
  // Probe on bit_extender_1_out
  assign bit_extender_1_out = {{31{1'b0}}, KeyboardStatus};  // Bit_Extender bit_extender_1
  assign bit_extender_2_out = {{25{1'b0}}, KeyboardData};  // Bit_Extender bit_extender_2
  Comparator #(.width(26)) comparator_2 (.a(AddressFromBus), .b(26'h3ffff14), .eq(comparator_1_eq[1]));  // open: gt, lt
  Multiplexer #(.select(3), .width(32)) multiplexer_1 (
    .in1(bit_extender_1_out), .in2(bit_extender_2_out), .out(DataToBus),
    .sel({WriteEnableFromBus, comparator_1_eq}));  // open: in0, in3, in4, in5, in6, in7
  // Probe on {WriteEnableFromBus, comparator_1_eq}
  and and_1 (KeyboardRead, WriteEnableFromBus, comparator_1_eq[0]);
  or or_1 (BusWriteEnable, comparator_1_eq[0], comparator_1_eq[1]);
endmodule

module RGBController (
  input  [31:0] DataFromBus,
  input  [25:0] AddressFromBus,
  input  WriteEnable,
  output [7:0] RGBX,
  output [7:0] RGBY,
  output [23:0] RGBColor,
  output RGBWrite
);

  wire clock_1_out, comparator_4_eq, demultiplexer_1_out9, demultiplexer_1_out10, demultiplexer_1_out12;
  wire [2:0] comparator_1_eq;
  wire [7:0] bit_extender_1_out;
  wire [23:0] bit_extender_2_out;

  Comparator #(.width(26)) comparator_1 (.a(AddressFromBus), .b(26'h3ffff20), .eq(comparator_1_eq[0]));  // open: gt, lt
  Comparator #(.width(26)) comparator_2 (.a(AddressFromBus), .b(26'h3ffff24), .eq(comparator_1_eq[1]));  // open: gt, lt
  Comparator #(.width(26)) comparator_3 (.a(AddressFromBus), .b(26'h3ffff28), .eq(comparator_1_eq[2]));  // open: gt, lt
  Comparator #(.width(26)) comparator_4 (.a(AddressFromBus), .b(26'h3ffff2c), .eq(comparator_4_eq));  // open: gt, lt
  Demultiplexer #(.select(4)) demultiplexer_1 (
    .out9(demultiplexer_1_out9), .out10(demultiplexer_1_out10), .out12(demultiplexer_1_out12), .in(1'b1),
    .sel({WriteEnable, comparator_1_eq}));  // open: out0, out1, out2, out3, out4, out5, out6, out7, out8, out11, out13, out14, out15
  // Probe on {WriteEnable, comparator_1_eq}
  Bit_Extender #(.in_width(32), .out_width(8), .\type ("zero")) bit_extender_1 (
    .in(DataFromBus), .out(bit_extender_1_out));
  Bit_Extender #(.in_width(32), .out_width(24), .\type ("zero")) bit_extender_2 (
    .in(DataFromBus), .out(bit_extender_2_out));
  Clock clock_1 (.out(clock_1_out));
  Register register_1 (.D(bit_extender_1_out), .en(demultiplexer_1_out9), .clk(clock_1_out), .Q(RGBX));  // open: clr
  Register register_2 (.D(bit_extender_1_out), .en(demultiplexer_1_out10), .clk(clock_1_out), .Q(RGBY));  // open: clr
  Register #(.width(24)) register_3 (
    .D(bit_extender_2_out), .en(demultiplexer_1_out12), .clk(clock_1_out), .Q(RGBColor));  // open: clr
  and and_1 (RGBWrite, WriteEnable, comparator_4_eq);

  // Notes on the sheet:
  //   10001
  //   10010
  //   10100
  //   11000
endmodule

module TerminalController (
  input  [31:0] DataFromBus,
  input  WriteEnableFromBus,
  input  [25:0] AddressFromBus,
  output [6:0] DataToTerminal,
  output WriteToTerminal
);

  wire comparator_1_eq;

  Comparator #(.width(26)) comparator_1 (.a(AddressFromBus), .b(26'h3ffff00), .eq(comparator_1_eq));  // open: gt, lt
  and and_1 (WriteToTerminal, WriteEnableFromBus, comparator_1_eq);

  assign DataToTerminal = DataFromBus[6:0];
endmodule

module CPU (
  input  [31:0] DataFromBus,
  output [31:0] DataToBus,
  output [25:0] AddressToBus,
  output BusWriteEnable
);

  wire alu_1_is_equal, and_1_out, and_2_out, clock_1_out, control_1_aluvsmem, control_1_beq, control_1_bne,
       control_1_imm_sel, control_1_j_select, control_1_jal_jalr, control_1_jr_jalr, control_1_reg_write_e,
       not_1_out, or_1_out, or_2_out, ram_1_p4, ram_1_p5;
  wire [4:0] control_1_alu_code, control_1_rd, control_1_rs, control_1_rt, multiplexer_6_out;
  wire [15:0] bit_extender_2_out, bit_extender_5_out;
  wire [25:0] bit_extender_3_out;
  wire [31:0] adder_1_out, adder_2_out, alu_1_res, bit_extender_1_out, control_1_imm, multiplexer_1_out,
       multiplexer_2_out, multiplexer_3_out, multiplexer_4_out, multiplexer_5_out, multiplexer_7_out,
       multiplexer_8_out, multiplier_1_out, PC_q, regfile_1_rs_data, rom_1_data, shifter_1_out,
       shifter_2_out, shifter_3_out, shifter_4_out;

  // Probe on multiplier_1_out
  Adder #(.width(32)) adder_1 (.a(PC_q), .b(32'h4), .out(adder_1_out));  // open: cin, cout
  Multiplier #(.mode("twosComplement"), .width(32)) multiplier_1 (
    .a(32'h4), .b(control_1_imm), .out(multiplier_1_out));  // open: cin, cout
  // Probe on adder_1_out
  Adder #(.width(32)) adder_2 (.a(adder_1_out), .b(multiplier_1_out), .out(adder_2_out));  // open: cin, cout
  // Probe on multiplier_1_out
  Multiplexer #(.width(32)) multiplexer_1 (
    .in0(adder_1_out), .in1(adder_2_out), .out(multiplexer_1_out), .sel(or_1_out));
  assign bit_extender_1_out = {{6{rom_1_data[25]}}, rom_1_data[25:0]};  // Bit_Extender bit_extender_1
  // Probe on rom_1_data[25:0]
  // Probe on multiplexer_3_out
  Shifter #(.width(32)) shifter_1 (.in(bit_extender_1_out), .\dist (5'b00010), .out(shifter_1_out));
  // Probe on regfile_1_rs_data
  Multiplexer #(.width(32)) multiplexer_2 (
    .in0(multiplexer_1_out), .in1(multiplexer_3_out), .out(multiplexer_2_out), .sel(control_1_j_select));
  Multiplexer #(.width(32)) multiplexer_3 (
    .in0(shifter_1_out), .in1(regfile_1_rs_data), .out(multiplexer_3_out), .sel(control_1_jr_jalr));
  Register #(.width(32)) PC (.D(multiplexer_2_out), .en(1'b1), .clk(clock_1_out), .Q(PC_q));  // open: clr
  Clock clock_1 (.out(clock_1_out));
  Shifter #(.shift("lr"), .width(32)) shifter_2 (.in(PC_q), .\dist (5'b00010), .out(shifter_2_out));
  ROM #(.addrWidth(16), .dataWidth(32)) rom_1 (.addr(bit_extender_2_out), .data(rom_1_data));
  Bit_Extender #(.in_width(32)) bit_extender_2 (.in(shifter_2_out), .out(bit_extender_2_out));
  or or_1 (or_1_out, and_2_out, and_1_out);
  and and_1 (and_1_out, alu_1_is_equal, control_1_beq);
  and and_2 (and_2_out, control_1_bne, not_1_out);
  Clock clock_2 ();  // open: out
  Multiplexer #(.width(32)) multiplexer_4 (
    .in0(alu_1_res), .in1(DataFromBus), .out(multiplexer_4_out), .sel(control_1_aluvsmem));
  not not_1 (not_1_out, alu_1_is_equal);
  // Probe on multiplexer_5_out
  Multiplexer #(.width(32)) multiplexer_5 (
    .in0(multiplexer_4_out), .in1(adder_1_out), .out(multiplexer_5_out), .sel(control_1_jal_jalr));
  or or_2 (or_2_out, control_1_beq, control_1_bne);
  // Probe on control_1_rd
  Multiplexer #(.width(5)) multiplexer_6 (
    .in0(control_1_rt), .in1(control_1_rd), .out(multiplexer_6_out), .sel(or_2_out));
  regfile regfile_1 (
    .rs(control_1_rs), .rt(multiplexer_6_out), .rd_select(control_1_rd), .write_e(control_1_reg_write_e),
    .rd_data(multiplexer_5_out), .rs_data(regfile_1_rs_data), .rt_data(DataToBus));
  // Probe on regfile_1_rs_data
  // Probe on DataToBus
  Control control_1 (
    .instr(rom_1_data), .j_select(control_1_j_select), .ALU_code(control_1_alu_code),
    .reg_write_e(control_1_reg_write_e), .Mem_WE(BusWriteEnable), .ALUvsMEM(control_1_aluvsmem),
    .bne(control_1_bne), .beq(control_1_beq), .rs(control_1_rs), .jr_jalr(control_1_jr_jalr),
    .jal_jalr(control_1_jal_jalr), .rt(control_1_rt), .rd(control_1_rd), .imm(control_1_imm),
    .imm_sel(control_1_imm_sel));
  // Probe on multiplexer_8_out
  Multiplexer #(.width(32)) multiplexer_7 (
    .in0(DataToBus), .in1(control_1_imm), .out(multiplexer_7_out), .sel(control_1_imm_sel));
  // Probe on control_1_imm
  // Probe on control_1_imm
  Multiplexer #(.width(32)) multiplexer_8 (
    .in0(multiplexer_7_out), .in1(DataToBus), .out(multiplexer_8_out), .sel(or_2_out));
  Shifter #(.shift("lr"), .width(32)) shifter_3 (.in(alu_1_res), .\dist (5'b00010), .out(shifter_3_out));
  ALU alu_1 (
    .OP1(regfile_1_rs_data), .OP2(multiplexer_8_out), .ALU_CODE(control_1_alu_code), .Res(alu_1_res),
    .is_equal(alu_1_is_equal));
  Bit_Extender #(.in_width(32), .out_width(26)) bit_extender_3 (.in(shifter_3_out), .out(bit_extender_3_out));
  // Probe on shifter_3_out
  // Probe on alu_1_res
  // Probe on bit_extender_3_out
  // Probe on alu_1_res
  Bit_Extender #(.in_width(32), .out_width(26)) bit_extender_4 (.in(alu_1_res), .out(AddressToBus));
  Bit_Extender #(.in_width(32)) bit_extender_5 (.in(shifter_4_out), .out(bit_extender_5_out));
  Shifter #(.shift("lr"), .width(32)) shifter_4 (.in(alu_1_res), .\dist (5'b00010), .out(shifter_4_out));
  // RAM #(.addrWidth(16), .dataWidth(32), .enables("line")) ram_1: pin names not known; wires that end beside it: BusWriteEnable, bit_extender_5_out, DataToBus, ram_1_p4, ram_1_p5
  Clock clock_3 (.out(ram_1_p4));

  // Notes on the sheet:
  //   immi
  //   rs
  //   J_select
  //   jr_jalr
  //   contents of rom_1 (hex, n*v repeats v):
  //   1040000d 201b0001 105b000f 201b0005 105b0027 201b0009 105b0046 201b000a 105b004c 201b000b 105b004b
  //   201b000c 105b004b 8000055 201df000 201b0000 ac1bf004 800006d 23bdfff4 afa80000 afa90004 afaa0008
  //   2008000a 23bb0000 10800008 23bdfffc 216b0004 88001a 4810 21290030 afa90000 2012 8000018 13bb0004
  //   8fa40000 23bd0004 ac04ff00 8000021 3aae820 8fa80000 8fa90004 8faa0008 23bd000c 3400008 20020000
  //   23bdffe4 afa80000 afa90004 afaa0008 afb0000c afb10010 afab0014 afac0018 2009000a 2010002f 2011003a
  //   200c0030 8c0aff14 20a582a 11600008 151582a 11600006 ac00ff10 14c5022 490018 1012 4a1020 8000039
  //   8fa80000 8fa90004 8faa0008 8fb0000c 8fb10010 8fab0014 8fac0018 23bd001c 3400008 20050004 8c1bf004
  //   23620000 85001a 2012 364d820 ac1bf004 3400008 8000055 ac04ff00 3400008 23bdfff0 afa90004 afab0008
  //   afb0000c afb10010 2009000a 20100030 2011003a 8c02ff14 50582a 15600003 222582a 15600001 8000060
  //   ac00ff10 8fa90004 8fab0008 8fb0000c 8fb10010 23bd0010 3400008 2008007f 20090000 200a02bc 200b0001
  //   200c0004 ac09ff40 ac0aff44 ac08ff48 ac0bff4c 118b0006 18b6022 21290001 ac09ff40 1485022 ac0aff44
  //   8000076 ac00ff4c
  //   is_equal
  //   beq
  //   bne
  //   not_is_equal
  //   delete this constant 0
endmodule

module Control (
  input  [31:0] instr,
  output j_select,
  output [4:0] ALU_code,
  output reg_write_e,
  output Mem_WE,
  output ALUvsMEM,
  output bne,
  output beq,
  output [4:0] rs,
  output jr_jalr,
  output jal_jalr,
  output [4:0] rt,
  output [4:0] rd,
  output [31:0] imm,
  output imm_sel
);

  wire and_2_out, comparator_1_eq, comparator_2_eq, comparator_5_eq, comparator_6_eq, comparator_7_lt,
       comparator_8_gt, comparator_9_lt, comparator_11_eq, comparator_14_eq, comparator_15_eq,
       comparator_16_eq, comparator_17_eq, comparator_18_eq;
  wire [1:0] comparator_1_gt, comparator_4_gt;
  wire [4:0] bit_extender_2_out, bit_extender_3_out, i_alusel_1_alucode, j_alusel_1_alucode,
       multiplexer_1_out, multiplexer_6_out, or_3_out, r_alusel_1_alucode;
  wire [15:0] bit_extender_1_out, demultiplexer_2_out0, demultiplexer_2_out1, demultiplexer_2_out2,
       multiplexer_3_out;
  wire [31:0] bit_extender_4_out, bit_extender_5_out, bit_extender_6_out, demultiplexer_1_out0,
       demultiplexer_1_out1, demultiplexer_1_out2;

  Demultiplexer #(.select(2), .width(32)) demultiplexer_1 (
    .out0(demultiplexer_1_out0), .out1(demultiplexer_1_out1), .out2(demultiplexer_1_out2), .in(instr),
    .sel(comparator_1_gt));  // open: out3
  Comparator #(.mode("unsigned"), .width(6)) comparator_1 (
    .a(instr[31:26]), .b(6'b000011), .gt(comparator_1_gt[0]), .eq(comparator_1_eq));  // open: lt
  Comparator #(.mode("unsigned"), .width(6)) comparator_2 (
    .a(instr[31:26]), .b(6'b000010), .eq(comparator_2_eq));  // open: gt, lt
  or or_1 (comparator_1_gt[1], comparator_1_eq, comparator_2_eq);
  assign bit_extender_1_out = {{11{1'b0}}, demultiplexer_1_out0[15:11]};  // Bit_Extender bit_extender_1
  R_ALUsel r_alusel_1 (.funcCode(demultiplexer_1_out0[5:0]), .ALUCode(r_alusel_1_alucode));
  I_ALUsel i_alusel_1 (.OPCode(demultiplexer_1_out1[31:26]), .ALUCode(i_alusel_1_alucode));
  Multiplexer #(.select(2), .width(5)) multiplexer_1 (
    .in0(demultiplexer_1_out0[25:21]), .in1(demultiplexer_1_out1[25:21]), .out(multiplexer_1_out),
    .sel(comparator_1_gt));  // open: in2, in3
  Multiplexer #(.select(2), .width(5)) multiplexer_2 (
    .in0(demultiplexer_1_out0[20:16]), .in1(demultiplexer_1_out1[20:16]), .out(rt), .sel(comparator_1_gt));  // open: in2, in3
  Comparator #(.mode("unsigned"), .width(2)) comparator_3 (
    .a(comparator_1_gt), .b(2'b00), .gt(comparator_4_gt[1]));  // open: eq, lt
  Comparator #(.mode("unsigned"), .width(5)) comparator_4 (
    .a(demultiplexer_1_out0[10:6]), .b({5{1'b0}}), .gt(comparator_4_gt[0]));  // open: eq, lt
  J_ALUsel j_alusel_1 (.OPCode(demultiplexer_1_out2[31:26]), .ALUCode(j_alusel_1_alucode));
  or or_2 (imm_sel, comparator_4_gt[1], comparator_4_gt[0]);
  // Probe on comparator_1_gt
  Multiplexer #(.select(2), .width(16)) multiplexer_3 (
    .in0(bit_extender_1_out), .in1(bit_extender_1_out), .in2(demultiplexer_1_out1[15:0]),
    .out(multiplexer_3_out), .sel(comparator_4_gt));  // open: in3
  // Probe on comparator_4_gt
  Multiplexer #(.select(2), .width(5)) multiplexer_4 (
    .in0(r_alusel_1_alucode), .in1(i_alusel_1_alucode), .in2(j_alusel_1_alucode), .out(ALU_code),
    .sel(comparator_1_gt));  // open: in3
  Comparator #(.width(5)) comparator_5 (
    .a({5{1'b0}}), .b(demultiplexer_1_out1[25:21]), .eq(comparator_5_eq));  // open: gt, lt
  Demultiplexer #(.select(2), .width(16)) demultiplexer_2 (
    .out0(demultiplexer_2_out0), .out1(demultiplexer_2_out1), .out2(demultiplexer_2_out2),
    .in(multiplexer_3_out), .sel(comparator_4_gt));  // open: out3
  Multiplexer #(.width(5)) multiplexer_5 (.in0(multiplexer_1_out), .in1(rt), .out(rs), .sel(comparator_4_gt[0]));
  Bit_Extender #(.in_width(16), .out_width(5), .\type ("zero")) bit_extender_2 (
    .in(demultiplexer_2_out1), .out(bit_extender_2_out));
  Multiplexer #(.width(5)) multiplexer_6 (
    .in0({5{1'b0}}), .in1(demultiplexer_1_out0[10:6]), .out(multiplexer_6_out), .sel(imm_sel));
  Bit_Extender #(.in_width(16), .out_width(5), .\type ("zero")) bit_extender_3 (
    .in(demultiplexer_2_out0), .out(bit_extender_3_out));
  assign bit_extender_4_out = {{16{demultiplexer_2_out2[15]}}, demultiplexer_2_out2};  // Bit_Extender bit_extender_4
  assign bit_extender_5_out = {{6{1'b0}}, demultiplexer_1_out2[25:0]};  // Bit_Extender bit_extender_5
  assign bit_extender_6_out = {{27{1'b0}}, multiplexer_6_out};  // Bit_Extender bit_extender_6
  assign or_3_out = bit_extender_2_out | bit_extender_3_out;  // OR_Gate or_3, 5 bits wide
  Multiplexer #(.select(2), .width(32)) multiplexer_7 (
    .in0(bit_extender_6_out), .in1(bit_extender_4_out), .in2(bit_extender_5_out), .out(imm),
    .sel(comparator_1_gt));  // open: in3
  // Probe on comparator_1_gt
  Comparator #(.width(5)) comparator_6 (.a(ALU_code), .b({5{1'b0}}), .eq(comparator_6_eq));  // open: gt, lt
  // AND_Gate and_1 has open pins: in0=comparator_6_eq, in1=comparator_5_eq, out=open
  Multiplexer #(.select(2), .width(5)) multiplexer_8 (
    .in0(or_3_out), .in1(demultiplexer_1_out1[20:16]), .out(rd), .sel(comparator_1_gt));  // open: in2, in3
  Comparator #(.mode("unsigned"), .width(5)) comparator_7 (
    .a(ALU_code), .b(5'b00010), .lt(comparator_7_lt));  // open: gt, eq
  Comparator #(.mode("unsigned"), .width(5)) comparator_8 (
    .a(ALU_code), .b(5'b00011), .gt(comparator_8_gt));  // open: eq, lt
  Comparator #(.mode("unsigned"), .width(5)) comparator_9 (
    .a(ALU_code), .b(5'b01101), .lt(comparator_9_lt));  // open: gt, eq
  Comparator #(.mode("unsigned"), .width(5)) comparator_10 (.a(ALU_code), .b(5'b10010), .eq(Mem_WE));  // open: gt, lt
  Comparator #(.mode("unsigned"), .width(5)) comparator_11 (
    .a(ALU_code), .b(5'b10011), .eq(comparator_11_eq));  // open: gt, lt
  Comparator #(.mode("unsigned"), .width(5)) comparator_12 (.a(ALU_code), .b(5'b10000), .eq(bne));  // open: gt, lt
  Comparator #(.mode("unsigned"), .width(5)) comparator_13 (.a(ALU_code), .b(5'b10001), .eq(beq));  // open: gt, lt
  Comparator #(.mode("unsigned"), .width(5)) comparator_14 (
    .a(ALU_code), .b(5'b01101), .eq(comparator_14_eq));  // open: gt, lt
  Comparator #(.mode("unsigned"), .width(5)) comparator_15 (
    .a(ALU_code), .b(5'b01110), .eq(comparator_15_eq));  // open: gt, lt
  Comparator #(.mode("unsigned"), .width(5)) comparator_16 (
    .a(ALU_code), .b(5'b10101), .eq(comparator_16_eq));  // open: gt, lt
  Comparator #(.mode("unsigned"), .width(5)) comparator_17 (
    .a(ALU_code), .b(5'b01111), .eq(comparator_17_eq));  // open: gt, lt
  and and_2 (and_2_out, comparator_8_gt, comparator_9_lt);
  or or_4 (reg_write_e, comparator_7_lt, and_2_out, comparator_17_eq, comparator_15_eq, comparator_11_eq);
  or or_5 (ALUvsMEM, comparator_11_eq, bne, 1'b0, beq);
  or or_6 (jr_jalr, comparator_14_eq, comparator_17_eq, comparator_15_eq);
  Comparator #(.mode("unsigned"), .width(5)) comparator_18 (
    .a(5'b10100), .b(ALU_code), .eq(comparator_18_eq));  // open: gt, lt
  or or_7 (jal_jalr, comparator_15_eq, comparator_17_eq, comparator_16_eq);
  or or_8 (j_select, comparator_18_eq, comparator_16_eq, comparator_17_eq, jr_jalr);

  // Notes on the sheet:
  //   R
  //   J
  //   I
  //   funcode
  //   shamt
  //   R: rd
  //   R: rt
  //   R: rs
  //   I: rt
  //   I: rs
  //   I: imme
  //   I: imme
  //   shamt
  //   sw
  //   lw
  //   jalr
  //   jal
  //   syscall
  //   bne
  //   beq
  //   jr
endmodule

module regfile (
  input  [4:0] rd_select,
  input  [31:0] rd_data,
  input  [4:0] rs,
  input  [4:0] rt,
  input  write_e,
  output [31:0] rs_data,
  output [31:0] rt_data
);

  wire and_1_out, and_2_out, and_3_out, and_4_out, and_5_out, and_6_out, and_7_out, and_8_out, and_9_out,
       and_10_out, and_11_out, and_12_out, and_13_out, and_14_out, and_15_out, and_16_out, and_17_out,
       and_18_out, and_19_out, and_20_out, and_21_out, and_22_out, and_23_out, and_24_out, and_25_out,
       and_26_out, and_27_out, and_28_out, and_29_out, and_30_out, and_31_out, and_32_out, clk_out,
       demultiplexer_1_out0, demultiplexer_1_out1, demultiplexer_1_out2, demultiplexer_1_out3,
       demultiplexer_1_out4, demultiplexer_1_out5, demultiplexer_1_out6, demultiplexer_1_out7,
       demultiplexer_1_out8, demultiplexer_1_out9, demultiplexer_1_out10, demultiplexer_1_out11,
       demultiplexer_1_out12, demultiplexer_1_out13, demultiplexer_1_out14, demultiplexer_1_out15,
       demultiplexer_1_out16, demultiplexer_1_out17, demultiplexer_1_out18, demultiplexer_1_out19,
       demultiplexer_1_out20, demultiplexer_1_out21, demultiplexer_1_out22, demultiplexer_1_out23,
       demultiplexer_1_out24, demultiplexer_1_out25, demultiplexer_1_out26, demultiplexer_1_out27,
       demultiplexer_1_out28, demultiplexer_1_out29, demultiplexer_1_out30, demultiplexer_1_out31;
  wire [31:0] Reg0_q, Reg1_q, Reg2_q, Reg3_q, Reg4_q, Reg5_q, Reg6_q, Reg7_q, Reg8_q, Reg9_q, Reg10_q,
       Reg11_q, Reg12_q, Reg13_q, Reg14_q, Reg15_q, Reg16_q, Reg17_q, Reg18_q, Reg19_q, Reg20_q, Reg21_q,
       Reg22_q, Reg23_q, Reg24_q, Reg25_q, Reg26_q, Reg27_q, Reg28_q, Reg29_q, Reg30_q, Reg31_q;

  Demultiplexer #(.select(5)) demultiplexer_1 (
    .out0(demultiplexer_1_out0), .out1(demultiplexer_1_out1), .out2(demultiplexer_1_out2),
    .out3(demultiplexer_1_out3), .out4(demultiplexer_1_out4), .out5(demultiplexer_1_out5),
    .out6(demultiplexer_1_out6), .out7(demultiplexer_1_out7), .out8(demultiplexer_1_out8),
    .out9(demultiplexer_1_out9), .out10(demultiplexer_1_out10), .out11(demultiplexer_1_out11),
    .out12(demultiplexer_1_out12), .out13(demultiplexer_1_out13), .out14(demultiplexer_1_out14),
    .out15(demultiplexer_1_out15), .out16(demultiplexer_1_out16), .out17(demultiplexer_1_out17),
    .out18(demultiplexer_1_out18), .out19(demultiplexer_1_out19), .out20(demultiplexer_1_out20),
    .out21(demultiplexer_1_out21), .out22(demultiplexer_1_out22), .out23(demultiplexer_1_out23),
    .out24(demultiplexer_1_out24), .out25(demultiplexer_1_out25), .out26(demultiplexer_1_out26),
    .out27(demultiplexer_1_out27), .out28(demultiplexer_1_out28), .out29(demultiplexer_1_out29),
    .out30(demultiplexer_1_out30), .out31(demultiplexer_1_out31), .in(1'b1), .sel(rd_select));
  Clock clock_1 ();  // open: out
  and and_1 (and_1_out, write_e, demultiplexer_1_out1);
  and and_2 (and_2_out, demultiplexer_1_out2, write_e);
  and and_3 (and_3_out, write_e, demultiplexer_1_out3);
  and and_4 (and_4_out, write_e, demultiplexer_1_out4);
  and and_5 (and_5_out, write_e, demultiplexer_1_out5);
  and and_6 (and_6_out, write_e, demultiplexer_1_out6);
  and and_7 (and_7_out, write_e, demultiplexer_1_out7);
  and and_8 (and_8_out, write_e, demultiplexer_1_out8);
  and and_9 (and_9_out, write_e, demultiplexer_1_out9);
  and and_10 (and_10_out, write_e, demultiplexer_1_out10);
  and and_11 (and_11_out, write_e, demultiplexer_1_out11);
  and and_12 (and_12_out, write_e, demultiplexer_1_out12);
  and and_13 (and_13_out, write_e, demultiplexer_1_out13);
  and and_14 (and_14_out, write_e, demultiplexer_1_out14);
  and and_15 (and_15_out, write_e, demultiplexer_1_out15);
  and and_16 (and_16_out, write_e, demultiplexer_1_out16);
  and and_17 (and_17_out, write_e, demultiplexer_1_out17);
  and and_18 (and_18_out, write_e, demultiplexer_1_out18);
  and and_19 (and_19_out, write_e, demultiplexer_1_out19);
  and and_20 (and_20_out, write_e, demultiplexer_1_out20);
  and and_21 (and_21_out, write_e, demultiplexer_1_out21);
  and and_22 (and_22_out, write_e, demultiplexer_1_out22);
  and and_23 (and_23_out, write_e, demultiplexer_1_out23);
  and and_24 (and_24_out, write_e, demultiplexer_1_out24);
  and and_25 (and_25_out, write_e, demultiplexer_1_out25);
  and and_26 (and_26_out, write_e, demultiplexer_1_out26);
  and and_27 (and_27_out, write_e, demultiplexer_1_out27);
  and and_28 (and_28_out, write_e, demultiplexer_1_out28);
  and and_29 (and_29_out, write_e, demultiplexer_1_out29);
  and and_30 (and_30_out, write_e, demultiplexer_1_out30);
  and and_31 (and_31_out, demultiplexer_1_out31, write_e);
  and and_32 (and_32_out, write_e, demultiplexer_1_out0);
  Clock clk (.out(clk_out));
  Register #(.width(32)) Reg0 (.D({32{1'b0}}), .en(and_32_out), .clk(clk_out), .Q(Reg0_q));  // open: clr
  Register #(.width(32)) Reg1 (.D(rd_data), .en(and_1_out), .clk(clk_out), .Q(Reg1_q));  // open: clr
  Register #(.width(32)) Reg2 (.D(rd_data), .en(and_2_out), .clk(clk_out), .Q(Reg2_q));  // open: clr
  // Probe on Reg2_q
  Register #(.width(32)) Reg3 (.D(rd_data), .en(and_3_out), .clk(clk_out), .Q(Reg3_q));  // open: clr
  Register #(.width(32)) Reg4 (.D(rd_data), .en(and_4_out), .clk(clk_out), .Q(Reg4_q));  // open: clr
  Register #(.width(32)) Reg5 (.D(rd_data), .en(and_5_out), .clk(clk_out), .Q(Reg5_q));  // open: clr
  Register #(.width(32)) Reg6 (.D(rd_data), .en(and_6_out), .clk(clk_out), .Q(Reg6_q));  // open: clr
  Register #(.width(32)) Reg7 (.D(rd_data), .en(and_7_out), .clk(clk_out), .Q(Reg7_q));  // open: clr
  Register #(.width(32)) Reg8 (.D(rd_data), .en(and_8_out), .clk(clk_out), .Q(Reg8_q));  // open: clr
  Register #(.width(32)) Reg9 (.D(rd_data), .en(and_9_out), .clk(clk_out), .Q(Reg9_q));  // open: clr
  Register #(.width(32)) Reg10 (.D(rd_data), .en(and_10_out), .clk(clk_out), .Q(Reg10_q));  // open: clr
  Register #(.width(32)) Reg11 (.D(rd_data), .en(and_11_out), .clk(clk_out), .Q(Reg11_q));  // open: clr
  Register #(.width(32)) Reg12 (.D(rd_data), .en(and_12_out), .clk(clk_out), .Q(Reg12_q));  // open: clr
  Register #(.width(32)) Reg13 (.D(rd_data), .en(and_13_out), .clk(clk_out), .Q(Reg13_q));  // open: clr
  Register #(.width(32)) Reg14 (.D(rd_data), .en(and_14_out), .clk(clk_out), .Q(Reg14_q));  // open: clr
  Register #(.width(32)) Reg15 (.D(rd_data), .en(and_15_out), .clk(clk_out), .Q(Reg15_q));  // open: clr
  Register #(.width(32)) Reg16 (.D(rd_data), .en(and_16_out), .clk(clk_out), .Q(Reg16_q));  // open: clr
  Register #(.width(32)) Reg17 (.D(rd_data), .en(and_17_out), .clk(clk_out), .Q(Reg17_q));  // open: clr
  Register #(.width(32)) Reg18 (.D(rd_data), .en(and_18_out), .clk(clk_out), .Q(Reg18_q));  // open: clr
  Register #(.width(32)) Reg19 (.D(rd_data), .en(and_19_out), .clk(clk_out), .Q(Reg19_q));  // open: clr
  Register #(.width(32)) Reg20 (.D(rd_data), .en(and_20_out), .clk(clk_out), .Q(Reg20_q));  // open: clr
  Register #(.width(32)) Reg21 (.D(rd_data), .en(and_21_out), .clk(clk_out), .Q(Reg21_q));  // open: clr
  Register #(.width(32)) Reg22 (.D(rd_data), .en(and_22_out), .clk(clk_out), .Q(Reg22_q));  // open: clr
  Register #(.width(32)) Reg23 (.D(rd_data), .en(and_23_out), .clk(clk_out), .Q(Reg23_q));  // open: clr
  Register #(.width(32)) Reg24 (.D(rd_data), .en(and_24_out), .clk(clk_out), .Q(Reg24_q));  // open: clr
  Register #(.width(32)) Reg25 (.D(rd_data), .en(and_25_out), .clk(clk_out), .Q(Reg25_q));  // open: clr
  Register #(.width(32)) Reg26 (.D(rd_data), .en(and_26_out), .clk(clk_out), .Q(Reg26_q));  // open: clr
  Register #(.width(32)) Reg27 (.D(rd_data), .en(and_27_out), .clk(clk_out), .Q(Reg27_q));  // open: clr
  Register #(.width(32)) Reg28 (.D(rd_data), .en(and_28_out), .clk(clk_out), .Q(Reg28_q));  // open: clr
  Register #(.width(32)) Reg29 (.D(rd_data), .en(and_29_out), .clk(clk_out), .Q(Reg29_q));  // open: clr
  Register #(.width(32)) Reg30 (.D(rd_data), .en(and_30_out), .clk(clk_out), .Q(Reg30_q));  // open: clr
  Register #(.width(32)) Reg31 (.D(rd_data), .en(and_31_out), .clk(clk_out), .Q(Reg31_q));  // open: clr
  // Probe on Reg4_q
  // Probe on Reg8_q
  // Probe on Reg29_q
  Multiplexer #(.select(5), .width(32)) multiplexer_1 (
    .in0(Reg0_q), .in1(Reg1_q), .in2(Reg2_q), .in3(Reg3_q), .in4(Reg4_q), .in5(Reg5_q), .in6(Reg6_q),
    .in7(Reg7_q), .in8(Reg8_q), .in9(Reg9_q), .in10(Reg10_q), .in11(Reg11_q), .in12(Reg12_q), .in13(Reg13_q),
    .in14(Reg14_q), .in15(Reg15_q), .in16(Reg16_q), .in17(Reg17_q), .in18(Reg18_q), .in19(Reg19_q),
    .in20(Reg20_q), .in21(Reg21_q), .in22(Reg22_q), .in23(Reg23_q), .in24(Reg24_q), .in25(Reg25_q),
    .in26(Reg26_q), .in27(Reg27_q), .in28(Reg28_q), .in29(Reg29_q), .in30(Reg30_q), .in31(Reg31_q),
    .out(rs_data), .sel(rs));
  Multiplexer #(.select(5), .width(32)) multiplexer_2 (
    .in0(Reg0_q), .in1(Reg1_q), .in2(Reg2_q), .in3(Reg3_q), .in4(Reg4_q), .in5(Reg5_q), .in6(Reg6_q),
    .in7(Reg7_q), .in8(Reg8_q), .in9(Reg9_q), .in10(Reg10_q), .in11(Reg11_q), .in12(Reg12_q), .in13(Reg13_q),
    .in14(Reg14_q), .in15(Reg15_q), .in16(Reg16_q), .in17(Reg17_q), .in18(Reg18_q), .in19(Reg19_q),
    .in20(Reg20_q), .in21(Reg21_q), .in22(Reg22_q), .in23(Reg23_q), .in24(Reg24_q), .in25(Reg25_q),
    .in26(Reg26_q), .in27(Reg27_q), .in28(Reg28_q), .in29(Reg29_q), .in30(Reg30_q), .in31(Reg31_q),
    .out(rt_data), .sel(rt));
endmodule

module ALU (
  input  [31:0] OP1,
  input  [31:0] OP2,
  input  [4:0] ALU_CODE,
  output is_equal,
  output [31:0] Res
);

  wire clock_2_out, comparator_2_lt, comparator_3_eq, comparator_4_eq, or_4_out;
  wire [4:0] bit_extender_1_out, bit_extender_2_out;
  wire [31:0] adder_1_out, and_32_out, bit_extender_3_out, divider_1_out, divider_1_rem, HI_q, LO_q,
       multiplexer_1_out, multiplexer_2_out, multiplier_1_cout, multiplier_1_out, nor_31_out, or_34_out,
       shifter_1_out, shifter_2_out, subtractor_1_out, xor_32_out;

  // Probe on OP1
  // Probe on OP2
  Comparator #(.width(32)) comparator_1 (.a(OP1), .b(OP2), .eq(is_equal));  // open: gt, lt
  // Probe on OP2
  Bit_Extender #(.in_width(32), .out_width(5)) bit_extender_1 (.in(OP2), .out(bit_extender_1_out));
  Bit_Extender #(.in_width(32), .out_width(5)) bit_extender_2 (.in(OP2), .out(bit_extender_2_out));
  Adder #(.width(32)) adder_1 (.a(OP1), .b(OP2), .out(adder_1_out));  // open: cin, cout
  Subtractor #(.width(32)) subtractor_1 (.a(OP1), .b(OP2), .out(subtractor_1_out));  // open: bin, bout
  Multiplier #(.width(32)) multiplier_1 (
    .a(OP1), .b(OP2), .out(multiplier_1_out), .cout(multiplier_1_cout));  // open: cin
  Divider #(.width(32)) divider_1 (.a(OP1), .b(OP2), .out(divider_1_out), .rem(divider_1_rem));  // open: upper
  Comparator #(.width(32)) comparator_2 (.a(OP1), .b(OP2), .lt(comparator_2_lt));  // open: gt, eq
  Clock clock_1 ();  // open: out
  Shifter #(.width(32)) shifter_1 (.in(OP1), .\dist (bit_extender_1_out), .out(shifter_1_out));
  Shifter #(.shift("lr"), .width(32)) shifter_2 (.in(OP1), .\dist (bit_extender_2_out), .out(shifter_2_out));
  and and_1 (and_32_out[31], OP1[31], OP2[31]);
  and and_2 (and_32_out[30], OP1[30], OP2[30]);
  and and_3 (and_32_out[29], OP1[29], OP2[29]);
  or or_1 (or_34_out[31], OP1[31], OP2[31]);
  Multiplexer #(.width(32)) multiplexer_1 (
    .in0(multiplier_1_out), .in1(divider_1_out), .out(multiplexer_1_out), .sel(comparator_3_eq));
  Multiplexer #(.width(32)) multiplexer_2 (
    .in0(multiplier_1_cout), .in1(divider_1_rem), .out(multiplexer_2_out), .sel(comparator_3_eq));
  // Probe on multiplexer_2_out
  Comparator #(.width(5)) comparator_3 (.a(5'b00011), .b(ALU_CODE), .eq(comparator_3_eq));  // open: gt, lt
  Comparator #(.width(5)) comparator_4 (.a(5'b00010), .b(ALU_CODE), .eq(comparator_4_eq));  // open: gt, lt
  and and_4 (and_32_out[28], OP1[28], OP2[28]);
  and and_5 (and_32_out[27], OP1[27], OP2[27]);
  or or_2 (or_34_out[30], OP1[30], OP2[30]);
  or or_3 (or_34_out[29], OP1[29], OP2[29]);
  nor nor_1 (nor_31_out[31], OP1[31], OP2[31]);
  nor nor_2 (nor_31_out[30], OP1[30], OP2[30]);
  xor xor_1 (xor_32_out[31], OP1[31], OP2[31]);
  // Probe on multiplexer_1_out
  or or_4 (or_4_out, comparator_3_eq, comparator_4_eq);
  Clock clock_2 (.out(clock_2_out));
  and and_6 (and_32_out[26], OP1[26], OP2[26]);
  and and_7 (and_32_out[25], OP1[25], OP2[25]);
  or or_5 (or_34_out[28], OP1[28], OP2[28]);
  or or_6 (or_34_out[27], OP1[27], OP2[27]);
  nor nor_3 (nor_31_out[29], OP1[29], OP2[29]);
  nor nor_4 (nor_31_out[28], OP1[28], OP2[28]);
  xor xor_2 (xor_32_out[30], OP1[30], OP2[30]);
  xor xor_3 (xor_32_out[29], OP1[29], OP2[29]);
  Register #(.width(32)) LO (.D(multiplexer_1_out), .en(or_4_out), .clk(clock_2_out), .Q(LO_q));  // open: clr
  Register #(.width(32)) HI (.D(multiplexer_2_out), .en(or_4_out), .clk(clock_2_out), .Q(HI_q));  // open: clr
  and and_8 (and_32_out[23], OP1[23], OP2[23]);
  and and_9 (and_32_out[24], OP1[24], OP2[24]);
  or or_7 (or_34_out[25], OP1[25], OP2[25]);
  or or_8 (or_34_out[26], OP1[26], OP2[26]);
  nor nor_5 (nor_31_out[26], OP1[26], OP2[26]);
  nor nor_6 (nor_31_out[27], OP1[27], OP2[27]);
  xor xor_4 (xor_32_out[27], OP1[27], OP2[27]);
  xor xor_5 (xor_32_out[28], OP1[28], OP2[28]);
  and and_10 (and_32_out[22], OP1[22], OP2[22]);
  and and_11 (and_32_out[21], OP1[21], OP2[21]);
  or or_9 (or_34_out[24], OP1[24], OP2[24]);
  or or_10 (or_34_out[23], OP1[23], OP2[23]);
  nor nor_7 (nor_31_out[25], OP1[25], OP2[25]);
  nor nor_8 (nor_31_out[24], OP1[24], OP2[24]);
  xor xor_6 (xor_32_out[26], OP1[26], OP2[26]);
  xor xor_7 (xor_32_out[25], OP1[25], OP2[25]);
  assign bit_extender_3_out = {{31{1'b0}}, comparator_2_lt};  // Bit_Extender bit_extender_3
  and and_12 (and_32_out[20], OP1[20], OP2[20]);
  and and_13 (and_32_out[19], OP1[19], OP2[19]);
  or or_11 (or_34_out[22], OP1[22], OP2[22]);
  or or_12 (or_34_out[21], OP1[21], OP2[21]);
  nor nor_9 (nor_31_out[23], OP1[23], OP2[23]);
  nor nor_10 (nor_31_out[22], OP1[22], OP2[22]);
  xor xor_8 (xor_32_out[24], OP1[24], OP2[24]);
  xor xor_9 (xor_32_out[23], OP1[23], OP2[23]);
  and and_14 (and_32_out[18], OP1[18], OP2[18]);
  and and_15 (and_32_out[17], OP1[17], OP2[17]);
  or or_13 (or_34_out[20], OP1[20], OP2[20]);
  or or_14 (or_34_out[19], OP1[19], OP2[19]);
  nor nor_11 (nor_31_out[21], OP1[21], OP2[21]);
  nor nor_12 (nor_31_out[20], OP1[20], OP2[20]);
  xor xor_10 (xor_32_out[22], OP1[22], OP2[22]);
  xor xor_11 (xor_32_out[21], OP1[21], OP2[21]);
  and and_16 (and_32_out[16], OP1[16], OP2[16]);
  and and_17 (and_32_out[15], OP1[15], OP2[15]);
  or or_15 (or_34_out[18], OP1[18], OP2[18]);
  or or_16 (or_34_out[17], OP1[17], OP2[17]);
  nor nor_13 (nor_31_out[19], OP1[19], OP2[19]);
  nor nor_14 (nor_31_out[18], OP1[18], OP2[18]);
  xor xor_12 (xor_32_out[20], OP1[20], OP2[20]);
  xor xor_13 (xor_32_out[19], OP1[19], OP2[19]);
  and and_18 (and_32_out[14], OP1[14], OP2[14]);
  and and_19 (and_32_out[13], OP1[13], OP2[13]);
  or or_17 (or_34_out[16], OP1[16], OP2[16]);
  or or_18 (or_34_out[15], OP1[15], OP2[15]);
  nor nor_15 (nor_31_out[17], OP1[17], OP2[17]);
  nor nor_16 (nor_31_out[16], OP1[16], OP2[16]);
  xor xor_14 (xor_32_out[18], OP1[18], OP2[18]);
  xor xor_15 (xor_32_out[17], OP1[17], OP2[17]);
  Multiplexer #(.select(5), .width(32)) multiplexer_3 (
    .in0(adder_1_out), .in1(subtractor_1_out), .in4(LO_q), .in5(HI_q), .in6(bit_extender_3_out),
    .in7(shifter_1_out), .in8(shifter_2_out), .in9(and_32_out), .in10(or_34_out), .in11(nor_31_out),
    .in12(xor_32_out), .in18(adder_1_out), .in19(adder_1_out), .out(Res), .sel(ALU_CODE));  // open: in2, in3, in13, in14, in15, in16, in17, in20, in21, in22, in23, in24, in25, in26, in27, in28, in29, in30, in31
  and and_20 (and_32_out[12], OP1[12], OP2[12]);
  and and_21 (and_32_out[11], OP1[11], OP2[11]);
  or or_19 (or_34_out[14], OP1[14], OP2[14]);
  or or_20 (or_34_out[13], OP1[13], OP2[13]);
  nor nor_17 (nor_31_out[15], OP1[15], OP2[15]);
  or or_21 (nor_31_out[14], OP1[14], OP2[14]);
  xor xor_16 (xor_32_out[16], OP1[16], OP2[16]);
  xor xor_17 (xor_32_out[15], OP1[15], OP2[15]);
  // Probe on ALU_CODE
  and and_22 (and_32_out[10], OP1[10], OP2[10]);
  and and_23 (and_32_out[9], OP1[9], OP2[9]);
  or or_22 (or_34_out[12], OP1[12], OP2[12]);
  or or_23 (or_34_out[11], OP1[11], OP2[11]);
  nor nor_18 (nor_31_out[13], OP1[13], OP2[13]);
  nor nor_19 (nor_31_out[12], OP1[12], OP2[12]);
  xor xor_18 (xor_32_out[14], OP1[14], OP2[14]);
  xor xor_19 (xor_32_out[13], OP1[13], OP2[13]);
  and and_24 (and_32_out[8], OP1[8], OP2[8]);
  and and_25 (and_32_out[7], OP1[7], OP2[7]);
  or or_24 (or_34_out[10], OP1[10], OP2[10]);
  or or_25 (or_34_out[9], OP1[9], OP2[9]);
  nor nor_20 (nor_31_out[11], OP1[11], OP2[11]);
  nor nor_21 (nor_31_out[10], OP1[10], OP2[10]);
  xor xor_20 (xor_32_out[12], OP1[12], OP2[12]);
  xor xor_21 (xor_32_out[11], OP1[11], OP2[11]);
  and and_26 (and_32_out[6], OP1[6], OP2[6]);
  and and_27 (and_32_out[5], OP1[5], OP2[5]);
  or or_26 (or_34_out[8], OP1[8], OP2[8]);
  or or_27 (or_34_out[7], OP1[7], OP2[7]);
  nor nor_22 (nor_31_out[9], OP1[9], OP2[9]);
  nor nor_23 (nor_31_out[8], OP1[8], OP2[8]);
  xor xor_22 (xor_32_out[10], OP1[10], OP2[10]);
  xor xor_23 (xor_32_out[9], OP1[9], OP2[9]);
  and and_28 (and_32_out[4], OP1[4], OP2[4]);
  and and_29 (and_32_out[3], OP1[3], OP2[3]);
  or or_28 (or_34_out[6], OP1[6], OP2[6]);
  or or_29 (or_34_out[5], OP1[5], OP2[5]);
  nor nor_24 (nor_31_out[7], OP1[7], OP2[7]);
  nor nor_25 (nor_31_out[6], OP1[6], OP2[6]);
  xor xor_24 (xor_32_out[8], OP1[8], OP2[8]);
  xor xor_25 (xor_32_out[7], OP1[7], OP2[7]);
  and and_30 (and_32_out[2], OP1[2], OP2[2]);
  and and_31 (and_32_out[1], OP1[1], OP2[1]);
  or or_30 (or_34_out[4], OP1[4], OP2[4]);
  or or_31 (or_34_out[3], OP1[3], OP2[3]);
  nor nor_26 (nor_31_out[5], OP1[5], OP2[5]);
  nor nor_27 (nor_31_out[4], OP1[4], OP2[4]);
  xor xor_26 (xor_32_out[6], OP1[6], OP2[6]);
  xor xor_27 (xor_32_out[5], OP1[5], OP2[5]);
  and and_32 (and_32_out[0], OP1[0], OP2[0]);
  or or_32 (or_34_out[2], OP1[2], OP2[2]);
  or or_33 (or_34_out[1], OP1[1], OP2[1]);
  nor nor_28 (nor_31_out[3], OP1[3], OP2[3]);
  nor nor_29 (nor_31_out[2], OP1[2], OP2[2]);
  xor xor_28 (xor_32_out[4], OP1[4], OP2[4]);
  xor xor_29 (xor_32_out[3], OP1[3], OP2[3]);
  or or_34 (or_34_out[0], OP1[0], OP2[0]);
  nor nor_30 (nor_31_out[1], OP1[1], OP2[1]);
  nor nor_31 (nor_31_out[0], OP1[0], OP2[0]);
  xor xor_30 (xor_32_out[2], OP1[2], OP2[2]);
  xor xor_31 (xor_32_out[1], OP1[1], OP2[1]);
  xor xor_32 (xor_32_out[0], OP1[0], OP2[0]);

  // Notes on the sheet:
  //   rs
  //   rt/imm
  //   add
  //   addi
  //   sub
  //   mult
  //   div
  //   slt
  //   sll
  //   srl
endmodule

module R_ALUsel (
  input  [5:0] funcCode,
  output [4:0] ALUCode
);

  wire comparator_1_eq, comparator_2_eq, comparator_3_eq, comparator_4_eq, comparator_5_eq, comparator_6_eq,
       comparator_7_eq, comparator_8_eq, comparator_9_eq, comparator_10_eq, comparator_11_eq,
       comparator_12_eq, comparator_13_eq, comparator_14_eq, comparator_15_eq, comparator_16_eq;
  wire [4:0] multiplexer_1_out, multiplexer_2_out, multiplexer_3_out, multiplexer_4_out, multiplexer_5_out,
       multiplexer_6_out, multiplexer_7_out, multiplexer_8_out, multiplexer_9_out, multiplexer_10_out,
       multiplexer_11_out, multiplexer_12_out, multiplexer_13_out, multiplexer_14_out, multiplexer_15_out,
       multiplexer_16_out;

  Comparator #(.width(6)) comparator_1 (.a(6'b100000), .b(funcCode), .eq(comparator_1_eq));  // open: gt, lt
  Comparator #(.width(6)) comparator_2 (.a(6'b100010), .b(funcCode), .eq(comparator_2_eq));  // open: gt, lt
  Comparator #(.width(6)) comparator_3 (.a(6'b011000), .b(funcCode), .eq(comparator_3_eq));  // open: gt, lt
  Comparator #(.width(6)) comparator_4 (.a(6'b011010), .b(funcCode), .eq(comparator_4_eq));  // open: gt, lt
  Comparator #(.width(6)) comparator_5 (.a(6'b010010), .b(funcCode), .eq(comparator_5_eq));  // open: gt, lt
  Comparator #(.width(6)) comparator_6 (.a(6'b010000), .b(funcCode), .eq(comparator_6_eq));  // open: gt, lt
  Comparator #(.width(6)) comparator_7 (.a(6'b101010), .b(funcCode), .eq(comparator_7_eq));  // open: gt, lt
  Comparator #(.width(6)) comparator_8 (.a({6{1'b0}}), .b(funcCode), .eq(comparator_8_eq));  // open: gt, lt
  Comparator #(.width(6)) comparator_9 (.a(6'b000010), .b(funcCode), .eq(comparator_9_eq));  // open: gt, lt
  Comparator #(.width(6)) comparator_10 (.a(6'b100100), .b(funcCode), .eq(comparator_10_eq));  // open: gt, lt
  Comparator #(.width(6)) comparator_11 (.a(6'b100101), .b(funcCode), .eq(comparator_11_eq));  // open: gt, lt
  Comparator #(.width(6)) comparator_12 (.a(6'b100111), .b(funcCode), .eq(comparator_12_eq));  // open: gt, lt
  Comparator #(.width(6)) comparator_13 (.a(6'b100110), .b(funcCode), .eq(comparator_13_eq));  // open: gt, lt
  Comparator #(.width(6)) comparator_14 (.a(6'b001000), .b(funcCode), .eq(comparator_14_eq));  // open: gt, lt
  Comparator #(.width(6)) comparator_15 (.a(6'b001001), .b(funcCode), .eq(comparator_15_eq));  // open: gt, lt
  Comparator #(.width(6)) comparator_16 (.a(6'b001100), .b(funcCode), .eq(comparator_16_eq));  // open: gt, lt
  Multiplexer #(.width(5)) multiplexer_1 (
    .in0({5{1'b0}}), .in1({5{1'b0}}), .out(multiplexer_1_out), .sel(comparator_1_eq));
  Multiplexer #(.width(5)) multiplexer_2 (
    .in0({5{1'b0}}), .in1(5'b00001), .out(multiplexer_2_out), .sel(comparator_2_eq));
  Multiplexer #(.width(5)) multiplexer_3 (
    .in0({5{1'b0}}), .in1(5'b00010), .out(multiplexer_3_out), .sel(comparator_3_eq));
  Multiplexer #(.width(5)) multiplexer_4 (
    .in0({5{1'b0}}), .in1(5'b00011), .out(multiplexer_4_out), .sel(comparator_4_eq));
  Multiplexer #(.width(5)) multiplexer_5 (
    .in0({5{1'b0}}), .in1(5'b00100), .out(multiplexer_5_out), .sel(comparator_5_eq));
  Multiplexer #(.width(5)) multiplexer_6 (
    .in0({5{1'b0}}), .in1(5'b00101), .out(multiplexer_6_out), .sel(comparator_6_eq));
  Multiplexer #(.width(5)) multiplexer_7 (
    .in0({5{1'b0}}), .in1(5'b00110), .out(multiplexer_7_out), .sel(comparator_7_eq));
  Multiplexer #(.width(5)) multiplexer_8 (
    .in0({5{1'b0}}), .in1(5'b00111), .out(multiplexer_8_out), .sel(comparator_8_eq));
  Multiplexer #(.width(5)) multiplexer_9 (
    .in0({5{1'b0}}), .in1(5'b01000), .out(multiplexer_9_out), .sel(comparator_9_eq));
  Multiplexer #(.width(5)) multiplexer_10 (
    .in0({5{1'b0}}), .in1(5'b01001), .out(multiplexer_10_out), .sel(comparator_10_eq));
  Multiplexer #(.width(5)) multiplexer_11 (
    .in0({5{1'b0}}), .in1(5'b01010), .out(multiplexer_11_out), .sel(comparator_11_eq));
  Multiplexer #(.width(5)) multiplexer_12 (
    .in0({5{1'b0}}), .in1(5'b01011), .out(multiplexer_12_out), .sel(comparator_12_eq));
  Multiplexer #(.width(5)) multiplexer_13 (
    .in0({5{1'b0}}), .in1(5'b01100), .out(multiplexer_13_out), .sel(comparator_13_eq));
  Multiplexer #(.width(5)) multiplexer_14 (
    .in0({5{1'b0}}), .in1(5'b01101), .out(multiplexer_14_out), .sel(comparator_14_eq));
  Multiplexer #(.width(5)) multiplexer_15 (
    .in0({5{1'b0}}), .in1(5'b01110), .out(multiplexer_15_out), .sel(comparator_15_eq));
  Multiplexer #(.width(5)) multiplexer_16 (
    .in0({5{1'b0}}), .in1(5'b01111), .out(multiplexer_16_out), .sel(comparator_16_eq));
  assign ALUCode = multiplexer_1_out | multiplexer_2_out | multiplexer_3_out | multiplexer_4_out | multiplexer_5_out | multiplexer_6_out | multiplexer_7_out | multiplexer_8_out | multiplexer_9_out | multiplexer_10_out | multiplexer_11_out | multiplexer_12_out | multiplexer_13_out | multiplexer_14_out | multiplexer_15_out | multiplexer_16_out;  // OR_Gate or_1, 5 bits wide
endmodule

module I_ALUsel (
  input  [5:0] OPCode,
  output [4:0] ALUCode
);

  wire comparator_1_eq, comparator_2_eq, comparator_3_eq, comparator_4_eq, comparator_5_eq, comparator_6_eq,
       comparator_7_eq, comparator_8_eq, comparator_9_eq;
  wire [4:0] multiplexer_1_out, multiplexer_2_out, multiplexer_3_out, multiplexer_4_out, multiplexer_5_out,
       multiplexer_6_out, multiplexer_7_out, multiplexer_8_out, multiplexer_9_out;

  Comparator #(.width(6)) comparator_1 (.a(6'b001000), .b({6{1'b0}}), .eq(comparator_1_eq));  // open: gt, lt
  Comparator #(.width(6)) comparator_2 (.a(6'b000101), .b(OPCode), .eq(comparator_2_eq));  // open: gt, lt
  Comparator #(.width(6)) comparator_3 (.a(6'b000100), .b(OPCode), .eq(comparator_3_eq));  // open: gt, lt
  Comparator #(.width(6)) comparator_4 (.a(6'b101011), .b(OPCode), .eq(comparator_4_eq));  // open: gt, lt
  Comparator #(.width(6)) comparator_5 (.a(6'b100011), .b(OPCode), .eq(comparator_5_eq));  // open: gt, lt
  Comparator #(.width(6)) comparator_6 (.a(6'b010010), .b(OPCode), .eq(comparator_6_eq));  // open: gt, lt
  Comparator #(.width(6)) comparator_7 (.a(6'b010011), .b(OPCode), .eq(comparator_7_eq));  // open: gt, lt
  Comparator #(.width(6)) comparator_8 (.a({6{1'b0}}), .b(6'b000001), .eq(comparator_8_eq));  // open: gt, lt
  Comparator #(.width(6)) comparator_9 (.a(6'b000010), .b(6'b000001), .eq(comparator_9_eq));  // open: gt, lt
  Multiplexer #(.width(5)) multiplexer_1 (
    .in0({5{1'b0}}), .in1({5{1'b0}}), .out(multiplexer_1_out), .sel(comparator_1_eq));
  Multiplexer #(.width(5)) multiplexer_2 (
    .in0({5{1'b0}}), .in1(5'b10000), .out(multiplexer_2_out), .sel(comparator_2_eq));
  Multiplexer #(.width(5)) multiplexer_3 (
    .in0({5{1'b0}}), .in1(5'b10001), .out(multiplexer_3_out), .sel(comparator_3_eq));
  Multiplexer #(.width(5)) multiplexer_4 (
    .in0({5{1'b0}}), .in1(5'b10010), .out(multiplexer_4_out), .sel(comparator_4_eq));
  Multiplexer #(.width(5)) multiplexer_5 (
    .in0({5{1'b0}}), .in1(5'b10011), .out(multiplexer_5_out), .sel(comparator_5_eq));
  Multiplexer #(.width(5)) multiplexer_6 (
    .in0({5{1'b0}}), .in1(5'b00101), .out(multiplexer_6_out), .sel(comparator_6_eq));
  Multiplexer #(.width(5)) multiplexer_7 (
    .in0({5{1'b0}}), .in1(5'b00110), .out(multiplexer_7_out), .sel(comparator_7_eq));
  Multiplexer #(.width(5)) multiplexer_8 (
    .in0({5{1'b0}}), .in1(5'b00111), .out(multiplexer_8_out), .sel(comparator_8_eq));
  Multiplexer #(.width(5)) multiplexer_9 (
    .in0({5{1'b0}}), .in1(5'b01000), .out(multiplexer_9_out), .sel(comparator_9_eq));
  assign ALUCode = multiplexer_1_out | multiplexer_2_out | multiplexer_3_out | multiplexer_4_out | multiplexer_5_out | multiplexer_6_out | multiplexer_7_out | multiplexer_8_out | multiplexer_9_out;  // OR_Gate or_1, 5 bits wide
endmodule

module J_ALUsel (
  input  [5:0] OPCode,
  output [4:0] ALUCode
);

  wire comparator_1_eq, comparator_2_eq, comparator_3_eq, comparator_4_eq, comparator_5_eq, comparator_6_eq,
       comparator_7_eq, comparator_8_eq, comparator_9_eq;
  wire [4:0] multiplexer_1_out, multiplexer_2_out, multiplexer_3_out, multiplexer_4_out, multiplexer_5_out,
       multiplexer_6_out, multiplexer_7_out, multiplexer_8_out, multiplexer_9_out;

  Comparator #(.width(6)) comparator_1 (.a(6'b001000), .b({6{1'b0}}), .eq(comparator_1_eq));  // open: gt, lt
  Comparator #(.width(6)) comparator_2 (.a(6'b000010), .b(OPCode), .eq(comparator_2_eq));  // open: gt, lt
  Comparator #(.width(6)) comparator_3 (.a(6'b000011), .b(OPCode), .eq(comparator_3_eq));  // open: gt, lt
  Comparator #(.width(6)) comparator_4 (.a(6'b101011), .b(6'b000001), .eq(comparator_4_eq));  // open: gt, lt
  Comparator #(.width(6)) comparator_5 (.a(6'b100011), .b(6'b000001), .eq(comparator_5_eq));  // open: gt, lt
  Comparator #(.width(6)) comparator_6 (.a(6'b010010), .b(6'b000001), .eq(comparator_6_eq));  // open: gt, lt
  Comparator #(.width(6)) comparator_7 (.a(6'b010011), .b(6'b000001), .eq(comparator_7_eq));  // open: gt, lt
  Comparator #(.width(6)) comparator_8 (.a({6{1'b0}}), .b(6'b000001), .eq(comparator_8_eq));  // open: gt, lt
  Comparator #(.width(6)) comparator_9 (.a(6'b000010), .b(6'b000001), .eq(comparator_9_eq));  // open: gt, lt
  Multiplexer #(.width(5)) multiplexer_1 (
    .in0({5{1'b0}}), .in1({5{1'b0}}), .out(multiplexer_1_out), .sel(comparator_1_eq));
  Multiplexer #(.width(5)) multiplexer_2 (
    .in0({5{1'b0}}), .in1(5'b10100), .out(multiplexer_2_out), .sel(comparator_2_eq));
  Multiplexer #(.width(5)) multiplexer_3 (
    .in0({5{1'b0}}), .in1(5'b10101), .out(multiplexer_3_out), .sel(comparator_3_eq));
  Multiplexer #(.width(5)) multiplexer_4 (
    .in0({5{1'b0}}), .in1(5'b10010), .out(multiplexer_4_out), .sel(comparator_4_eq));
  Multiplexer #(.width(5)) multiplexer_5 (
    .in0({5{1'b0}}), .in1(5'b10011), .out(multiplexer_5_out), .sel(comparator_5_eq));
  Multiplexer #(.width(5)) multiplexer_6 (
    .in0({5{1'b0}}), .in1(5'b00101), .out(multiplexer_6_out), .sel(comparator_6_eq));
  Multiplexer #(.width(5)) multiplexer_7 (
    .in0({5{1'b0}}), .in1(5'b00110), .out(multiplexer_7_out), .sel(comparator_7_eq));
  Multiplexer #(.width(5)) multiplexer_8 (
    .in0({5{1'b0}}), .in1(5'b00111), .out(multiplexer_8_out), .sel(comparator_8_eq));
  Multiplexer #(.width(5)) multiplexer_9 (
    .in0({5{1'b0}}), .in1(5'b01000), .out(multiplexer_9_out), .sel(comparator_9_eq));
  assign ALUCode = multiplexer_1_out | multiplexer_2_out | multiplexer_3_out | multiplexer_4_out | multiplexer_5_out | multiplexer_6_out | multiplexer_7_out | multiplexer_8_out | multiplexer_9_out;  // OR_Gate or_1, 5 bits wide
endmodule

module RGBLEDControl (
  input  [31:0] DataFromBus,
  input  [25:0] AddressFromBus,
  input  WriteEnable,
  output Blue,
  output Green,
  output Red
);

  wire clock_1_out, demultiplexer_1_out9, demultiplexer_1_out10, demultiplexer_1_out12;
  wire [2:0] comparator_1_eq;
  wire [31:0] register_1_q, register_2_q, register_3_q;

  // Probe on 26'h3ffff3c
  Comparator #(.width(26)) comparator_1 (.a(AddressFromBus), .b(26'h3ffff34), .eq(comparator_1_eq[0]));  // open: gt, lt
  Comparator #(.width(26)) comparator_2 (.a(AddressFromBus), .b(26'h3ffff38), .eq(comparator_1_eq[1]));  // open: gt, lt
  // Probe on 26'h3ffff38
  Comparator #(.width(26)) comparator_3 (.a(AddressFromBus), .b(26'h3ffff3c), .eq(comparator_1_eq[2]));  // open: gt, lt
  Demultiplexer #(.select(4)) demultiplexer_1 (
    .out9(demultiplexer_1_out9), .out10(demultiplexer_1_out10), .out12(demultiplexer_1_out12), .in(1'b1),
    .sel({WriteEnable, comparator_1_eq}));  // open: out0, out1, out2, out3, out4, out5, out6, out7, out8, out11, out13, out14, out15
  // Probe on {WriteEnable, comparator_1_eq}
  Clock clock_1 (.out(clock_1_out));
  Register #(.width(32)) register_1 (
    .D(DataFromBus), .en(demultiplexer_1_out9), .clk(clock_1_out), .Q(register_1_q));  // open: clr
  Register #(.width(32)) register_2 (
    .D(DataFromBus), .en(demultiplexer_1_out10), .clk(clock_1_out), .Q(register_2_q));  // open: clr
  Register #(.width(32)) register_3 (
    .D(DataFromBus), .en(demultiplexer_1_out12), .clk(clock_1_out), .Q(register_3_q));  // open: clr
  Bit_Extender #(.in_width(32), .out_width(1)) bit_extender_1 (.in(register_1_q), .out(Blue));
  Bit_Extender #(.in_width(32), .out_width(1)) bit_extender_2 (.in(register_2_q), .out(Green));
  Bit_Extender #(.in_width(32), .out_width(1)) bit_extender_3 (.in(register_3_q), .out(Red));

  // Notes on the sheet:
  //   1001
  //   1010
  //   1100
endmodule

module HexDisplayController (
  input  WriteEnableFromBus,
  input  [31:0] DataFromBus,
  input  [25:0] AddressFromBus,
  output [3:0] DataToScreen
);

  wire and_1_out, comparator_1_eq;
  wire [3:0] bit_extender_1_out;

  Comparator #(.mode("unsigned"), .width(26)) comparator_1 (
    .a(AddressFromBus), .b(26'h3ffff30), .eq(comparator_1_eq));  // open: gt, lt
  Bit_Extender #(.in_width(32), .out_width(4), .\type ("zero")) bit_extender_1 (
    .in(DataFromBus), .out(bit_extender_1_out));
  Multiplexer #(.width(4)) multiplexer_1 (.in0(4'b0000), .in1(bit_extender_1_out), .out(DataToScreen), .sel(and_1_out));
  and and_1 (and_1_out, WriteEnableFromBus, comparator_1_eq);
endmodule

module SpeakerController (
  input  [31:0] DataFromBus,
  input  [25:0] AddressFromBus,
  input  WriteEnabled,
  output PlayMusic,
  output [1:0] ToneSelect,
  output [13:0] Hz,
  output [6:0] Volume
);

  wire clock_1_out, demultiplexer_1_out3, demultiplexer_1_out5, demultiplexer_1_out9, demultiplexer_1_out17;
  wire [4:1] comparator_4_eq;
  wire [31:0] MHz_q, OnOff_q, Tone_q, Vol_q;

  Demultiplexer #(.select(5)) demultiplexer_1 (
    .out3(demultiplexer_1_out3), .out5(demultiplexer_1_out5), .out9(demultiplexer_1_out9),
    .out17(demultiplexer_1_out17), .in(1'b1), .sel({comparator_4_eq, WriteEnabled}));  // open: out0, out1, out2, out4, out6, out7, out8, out10, out11, out12, out13, out14, out15, out16, out18, out19, out20, out21, out22, out23, out24, out25, out26, out27, out28, out29, out30, out31
  Clock clock_1 (.out(clock_1_out));
  Register #(.width(32)) OnOff (
    .D(DataFromBus), .en(demultiplexer_1_out3), .clk(clock_1_out), .Q(OnOff_q));  // open: clr
  Register #(.width(32)) Tone (
    .D(DataFromBus), .en(demultiplexer_1_out17), .clk(clock_1_out), .Q(Tone_q));  // open: clr
  Register #(.width(32)) MHz (.D(DataFromBus), .en(demultiplexer_1_out9), .clk(clock_1_out), .Q(MHz_q));  // open: clr
  Register #(.width(32)) Vol (.D(DataFromBus), .en(demultiplexer_1_out5), .clk(clock_1_out), .Q(Vol_q));  // open: clr
  // Probe on {comparator_4_eq, WriteEnabled}
  // Probe on 26'h3ffff40
  // Probe on 26'h3ffff48
  // Probe on 26'h3ffff4c
  Comparator #(.width(26)) comparator_1 (.a(AddressFromBus), .b(26'h3ffff40), .eq(comparator_4_eq[4]));  // open: gt, lt
  Comparator #(.width(26)) comparator_2 (.a(AddressFromBus), .b(26'h3ffff44), .eq(comparator_4_eq[3]));  // open: gt, lt
  Comparator #(.width(26)) comparator_3 (.a(AddressFromBus), .b(26'h3ffff48), .eq(comparator_4_eq[2]));  // open: gt, lt
  Comparator #(.width(26)) comparator_4 (.a(AddressFromBus), .b(26'h3ffff4c), .eq(comparator_4_eq[1]));  // open: gt, lt
  Bit_Extender #(.in_width(32), .out_width(1)) bit_extender_1 (.in(OnOff_q), .out(PlayMusic));
  Bit_Extender #(.in_width(32), .out_width(2)) bit_extender_2 (.in(Tone_q), .out(ToneSelect));
  Bit_Extender #(.in_width(32), .out_width(14)) bit_extender_3 (.in(MHz_q), .out(Hz));
  Bit_Extender #(.in_width(32), .out_width(7)) bit_extender_4 (.in(Vol_q), .out(Volume));
endmodule
